# Fritzing sketch diagram (saved by Fritzing 0.8.7b)

parts:
  Part1 = Arduino Nano (Rev3.0)  # not connected
  VCC1 = Battery
  X1 = USB Connectors [package=usb-microb]

nets:
  N1: VCC1.-, X1.D-
  N2: VCC1.+, X1.D+
